# Fritzing sketch esp32-cam_ftdi (saved by Fritzing 0.9.3b)
circuit board: 8.46667cm x 5.64444cm

parts:
  Часть1 = FTDI Basic Programmer
  Mod1 = ESP32 - CAM

nets:
  N1: Часть1.RXI, Mod1.VOR
  N2: Часть1.TXO, Mod1.VOT
  N3: Часть1.POWER, Mod1.5V
  GND: Часть1.GND, Mod1.GND, Mod1.IO0

custom parts:
  ESP32 - CAM: The ESP32-CAM has a very competitive small-size camera module that can operate independently as a minimum system with a footprint of only 27*40.5*4.5mm and a deep sleep current of up to 6mA.
