# Fritzing sketch esp32-cam_uno (saved by Fritzing 0.9.3b)

parts:
  Mod1 = ESP32 - CAM
  Часть1 = Arduino Uno (Rev3) - ICSP

nets:
  5V: Mod1.5V, Часть1.5V
  GND: Mod1.GND, Mod1.IO0, Часть1.GND, Часть1.RESET
  N1: Mod1.VOT, Часть1.D1/TX
  N2: Mod1.VOR, Часть1.D0/RX

custom parts:
  ESP32 - CAM: The ESP32-CAM has a very competitive small-size camera module that can operate independently as a minimum system with a footprint of only 27*40.5*4.5mm and a deep sleep current of up to 6mA.
