# Fritzing sketch full (saved by Fritzing 0.9.3b)
breadboards: 1

parts:
  Часть1 = Arduino Uno (Rev3) - ICSP
  S1 = H-Bridge with L298N
  Mod1 = ESP32 - CAM
  M1 = DC Motor
  M2 = DC Motor
  J1 = Basic Servo
  LED1 = smd LED [color="White (8000K)" package="0603 [SMD]"]
  LED2 = smd LED [color="White (8000K)" package="0603 [SMD]"]
  S2 = Pushbutton [package="[SMD]"]

nets:
  N1: Часть1.D8, S1.IN1
  N2: Часть1.D9_PWM, J1.pulse
  N3: Часть1.D10_PWM/SS, Mod1.VOT
  N4: Часть1.D11_PWM/MOSI, Mod1.VOR
  GND: Часть1.GND, Часть1.RESET, Mod1.GND, J1.gnd, LED1.cathode, LED2.cathode, S2.Pin_1, S2.Pin_2
  N5: Часть1.D2, LED1.anode, LED2.anode
  N6: Часть1.D3_PWM, S1.IN4
  N7: Часть1.D4, S1.IN3
  N8: Часть1.D5_PWM, S1.ENB
  N9: Часть1.D6_PWM, S1.ENA
  N10: Часть1.D7, S1.IN2
  5V: Часть1.5V, Mod1.5V, J1.vcc
  N11: S1.M1-01, M1.pin_2
  N12: S1.M1-02, M1.pin_1
  N13: S1.M2-01, M2.pin_2
  N14: S1.M2-02, M2.pin_1
  N15: Mod1.IO0, S2.Pin_3, S2.Pin_4

custom parts:
  H-Bridge with L298N: h-bridge
  ESP32 - CAM: The ESP32-CAM has a very competitive small-size camera module that can operate independently as a minimum system with a footprint of only 27*40.5*4.5mm and a deep sleep current of up to 6mA.
