# Fritzing sketch servo_uno (saved by Fritzing 0.9.3b)

parts:
  Часть2 = Arduino Uno (Rev3)
  J1 = Basic Servo

nets:
  N1: Часть2.D10_PWM/SS, J1.pulse
  5V: Часть2.5V, J1.vcc
  GND: Часть2.GND, J1.gnd
